// Digital circuit 1-Bit-Komperator.dig as structural Verilog
module _1_Bit_Komperator (
  input  x,
  input  y,
  input  ENL,
  output lt,
  output eq,
  output gt
);

  wire and_1_out, and_2_out, xnor_1_out;

  and and_1 (and_1_out, y, ~x);  // And
  xnor xnor_1 (xnor_1_out, y, x);
  and and_2 (and_2_out, ~y, x);  // And
  and and_3 (lt, and_1_out, ENL);
  and and_4 (eq, xnor_1_out, ENL);
  and and_5 (gt, and_2_out, ENL);
endmodule
