// Digital circuit 8-Bit-ALU.dig as structural Verilog
module _8_Bit_ALU (
  input  [7:0] A,
  input  [7:0] B,
  input  c_IN,
  input  INVA,
  input  ENA,
  input  ENB,
  input  F0,
  input  F1,
  output [7:0] \output ,
  output carry_out
);

  wire alu_1_carry_out, alu_2_carry_out, alu_3_carry_out, alu_4_carry_out, alu_5_carry_out, alu_6_carry_out,
       alu_7_carry_out;

  ALU alu_1 (
    .INVA(INVA), .A(A[0]), .ENA(ENA), .B(B[0]), .ENB(ENB), .CarryIn(c_IN), .F0(F0), .F1(F1),
    .\output (\output [0]), .carry_out(alu_1_carry_out));
  ALU alu_2 (
    .INVA(INVA), .A(A[1]), .ENA(ENA), .B(B[1]), .ENB(ENB), .CarryIn(alu_1_carry_out), .F0(F0), .F1(F1),
    .\output (\output [1]), .carry_out(alu_2_carry_out));
  ALU alu_3 (
    .INVA(INVA), .A(A[2]), .ENA(ENA), .B(B[2]), .ENB(ENA), .CarryIn(alu_2_carry_out), .F0(F0), .F1(F1),
    .\output (\output [2]), .carry_out(alu_3_carry_out));
  ALU alu_4 (
    .INVA(INVA), .A(A[3]), .ENA(ENA), .B(B[3]), .ENB(ENB), .CarryIn(alu_3_carry_out), .F0(F0), .F1(F1),
    .\output (\output [3]), .carry_out(alu_4_carry_out));
  ALU alu_5 (
    .INVA(INVA), .A(A[4]), .ENA(ENA), .B(B[4]), .ENB(ENB), .CarryIn(alu_4_carry_out), .F0(F0), .F1(F1),
    .\output (\output [4]), .carry_out(alu_5_carry_out));
  ALU alu_6 (
    .INVA(INVA), .A(A[5]), .ENA(ENA), .B(B[5]), .ENB(ENB), .CarryIn(alu_5_carry_out), .F0(F0), .F1(F1),
    .\output (\output [5]), .carry_out(alu_6_carry_out));
  ALU alu_7 (
    .INVA(INVA), .A(A[6]), .ENA(ENA), .B(B[6]), .ENB(ENB), .CarryIn(alu_6_carry_out), .F0(F0), .F1(F1),
    .\output (\output [6]), .carry_out(alu_7_carry_out));
  ALU alu_8 (
    .INVA(INVA), .A(A[7]), .ENA(ENA), .B(B[7]), .ENB(ENB), .CarryIn(alu_7_carry_out), .F0(F0), .F1(F1),
    .\output (\output [7]), .carry_out(carry_out));
endmodule
