// Digital circuit 8-Bit-Zählregister.dig as structural Verilog
module \_8_Bit_Zählregister  (
  input  [7:0] A_IN,
  input  INC,
  input  EN,
  input  CLK,
  input  RST,
  output [7:0] A_out
);

  wire [7:0] _8_bit_alu_1_output, multiplexer_1_out;

  _8_Bit_ALU _8_bit_alu_1 (
    .A(A_out), .B(8'h1), .c_IN(1'b0), .INVA(1'b0), .ENA(1'b1), .ENB(1'b1), .F0(1'b1), .F1(1'b1),
    .\output (_8_bit_alu_1_output));  // open: carry_out
  Multiplexer #(.Bits(8)) multiplexer_1 (.sel(INC), .in_0(A_IN), .in_1(_8_bit_alu_1_output), .out(multiplexer_1_out));
  _8_Bit_Register _8_bit_register_1 (.D_IN(multiplexer_1_out), .EN(EN), .CLK(CLK), .RST(RST), .D_OUT(A_out));
endmodule
