// Digital circuit ALU.dig as structural Verilog
module ALU (
  input  INVA,
  input  A,
  input  ENA,
  input  B,
  input  ENB,
  input  CarryIn,
  input  F0,
  input  F1,
  output \output ,
  output carry_out
);

  wire and_1_out, and_2_out, dekodierer_1_e_0, dekodierer_1_e_1, dekodierer_1_e_2, dekodierer_1_e_3,
       logikeinheit_1_and, logikeinheit_1_not, logikeinheit_1_or, volladdierer_enable_1_s_i, xor_1_out;

  and and_1 (and_1_out, A, ENA);
  and and_2 (and_2_out, B, ENB);
  xor xor_1 (xor_1_out, INVA, and_1_out);
  Dekodierer dekodierer_1 (
    .F0(F0), .F1(F1), .e_0(dekodierer_1_e_0), .e_1(dekodierer_1_e_1), .e_2(dekodierer_1_e_2),
    .e_3(dekodierer_1_e_3));
  Logikeinheit logikeinheit_1 (
    .a(xor_1_out), .b(and_2_out), .e_and(dekodierer_1_e_0), .e_or(dekodierer_1_e_1),
    .e_not(dekodierer_1_e_2), .AND(logikeinheit_1_and), .OR(logikeinheit_1_or), .NOT(logikeinheit_1_not));
  Volladdierer_enable volladdierer_enable_1 (
    .a_i(xor_1_out), .b_i(and_2_out), .c_i(CarryIn), .EN(dekodierer_1_e_3), .s_i(volladdierer_enable_1_s_i),
    .c_i_plus_1(carry_out));
  or or_1 (\output , logikeinheit_1_and, logikeinheit_1_or, logikeinheit_1_not, volladdierer_enable_1_s_i);
endmodule
