// Digital circuit ALU_8Bit_Complete_Computer.dig as structural Verilog
module ALU_8Bit_Complete_Computer (
  input  [4:0] CTRL,
  input  [7:0] A,
  input  [7:0] B,
  input  C_IN,
  output [7:0] OUT,
  output C_OUT
);

  _8_Bit_ALU _8_bit_alu_1 (
    .A(A), .B(B), .c_IN(C_IN), .INVA(CTRL[0]), .ENA(CTRL[1]), .ENB(CTRL[2]), .F0(CTRL[3]), .F1(CTRL[4]),
    .\output (OUT), .carry_out(C_OUT));
  // Pins of 1 and 8 bits meet at OUT
endmodule
