// Digital circuit Dekodierer.dig as structural Verilog
module Dekodierer (
  input  F0,
  input  F1,
  output e_0,
  output e_1,
  output e_2,
  output e_3
);

  wire not_1_out, not_2_out, not_3_out, not_4_out;

  not not_1 (not_1_out, F0);
  not not_2 (not_2_out, F1);
  not not_3 (not_3_out, F0);
  not not_4 (not_4_out, F1);
  and and_1 (e_0, not_1_out, not_2_out);
  and and_2 (e_1, not_3_out, F1);
  and and_3 (e_2, F0, not_4_out);
  and and_4 (e_3, F0, F1);
endmodule
