// Digital circuit Logikeinheit.dig as structural Verilog
module Logikeinheit (
  input  a,
  input  b,
  input  e_and,
  input  e_or,
  input  e_not,
  output AND,
  output OR,
  output NOT
);

  wire and_1_out, not_1_out, or_1_out;

  and and_1 (and_1_out, a, b);
  or or_1 (or_1_out, a, b);
  not not_1 (not_1_out, b);
  and and_2 (AND, and_1_out, e_and);
  and and_3 (OR, or_1_out, e_or);
  and and_4 (NOT, not_1_out, e_not);
endmodule
