// Digital circuit Steuerwerk.dig as structural Verilog
module Steuerwerk (
  input  [7:0] INSTR,
  input  CLK,
  input  RST,
  output FETCH_IR,
  output FETCH_AR,
  output EXECUTE,
  output [4:0] ALU_CTRL,
  output ALU_Carry,
  output Akku_EN,
  output PC_INC,
  output PC_EN,
  output ADRMUX,
  output RAM_W
);

  wire and_2_out, demultiplexer_1_out_0, demultiplexer_1_out_1, demultiplexer_1_out_2, demultiplexer_1_out_3,
       demultiplexer_1_out_4, demultiplexer_1_out_5, not_1_out, or_2_out;

  not not_1 (not_1_out, CLK);
  Demultiplexer #(.Selector_Bits(3)) demultiplexer_1 (
    .sel(INSTR[7:5]), .in(1'b1), .out_0(demultiplexer_1_out_0), .out_1(demultiplexer_1_out_1),
    .out_2(demultiplexer_1_out_2), .out_3(demultiplexer_1_out_3), .out_4(demultiplexer_1_out_4),
    .out_5(demultiplexer_1_out_5));  // open: out_6, out_7
  or or_1 (ALU_Carry, demultiplexer_1_out_1, demultiplexer_1_out_3);
  or or_2 (or_2_out, demultiplexer_1_out_0, demultiplexer_1_out_1, demultiplexer_1_out_2, demultiplexer_1_out_3);
  // Seq seq_1: pin names not known; wires that end beside it: EXECUTE, RST, FETCH_AR, not_1_out, FETCH_IR
  and and_1 (Akku_EN, EXECUTE, or_2_out);
  and and_2 (and_2_out, EXECUTE, demultiplexer_1_out_5);
  and and_3 (RAM_W, EXECUTE, demultiplexer_1_out_4);
  or or_3 (PC_INC, FETCH_IR, FETCH_AR);
  or or_4 (PC_EN, FETCH_IR, FETCH_AR, and_2_out);
  or or_5 (ADRMUX, FETCH_IR, FETCH_AR);

  assign ALU_CTRL = INSTR[4:0];
endmodule
