// Digital circuit Steuerwerk3.dig as structural Verilog
module Steuerwerk3 (
  input  [7:0] INSTR,
  input  CLK,
  input  RST,
  output FETCH_IR,
  output FETCH_AR,
  output EXECUTE,
  output [4:0] ALU_CTRL,
  output ALU_Carry,
  output Akku_EN,
  output PC_INC,
  output PC_EN,
  output ADRMUX,
  output RAM_W
);

  wire and_1_out, demultiplexer_1_out_0, demultiplexer_1_out_1, demultiplexer_1_out_2, demultiplexer_1_out_3,
       demultiplexer_1_out_4, demultiplexer_1_out_5, not_1_out, or_2_out;

  Demultiplexer #(.Selector_Bits(3)) demultiplexer_1 (
    .sel(INSTR[7:5]), .in(1'b1), .out_0(demultiplexer_1_out_0), .out_1(demultiplexer_1_out_1),
    .out_2(demultiplexer_1_out_2), .out_3(demultiplexer_1_out_3), .out_4(demultiplexer_1_out_4),
    .out_5(demultiplexer_1_out_5));  // open: out_6, out_7
  or or_1 (ALU_Carry, demultiplexer_1_out_1, demultiplexer_1_out_3);
  or or_2 (or_2_out, demultiplexer_1_out_0, demultiplexer_1_out_1, demultiplexer_1_out_2, demultiplexer_1_out_3);
  not not_1 (not_1_out, CLK);
  // Sequencer sequencer_1: pin names not known; wires that end beside it: EXECUTE, RST, FETCH_AR, not_1_out, FETCH_IR
  and and_1 (and_1_out, EXECUTE, demultiplexer_1_out_5);
  and and_2 (Akku_EN, EXECUTE, or_2_out);
  or or_3 (PC_INC, FETCH_IR, FETCH_AR);
  or or_4 (PC_EN, FETCH_IR, FETCH_AR, and_1_out);
  or or_5 (ADRMUX, FETCH_IR, FETCH_AR);
  and and_3 (RAM_W, EXECUTE, demultiplexer_1_out_4);

  assign ALU_CTRL = INSTR[4:0];
endmodule
