// Digital circuit Volladdierer.dig as structural Verilog
module Volladdierer (
  input  a_i,
  input  b_i,
  input  c_i,
  output s_i,
  output c_i_plus_1
);

  wire halbaddierer_1_c, halbaddierer_1_s, halbaddierer_2_c;

  Halbaddierer halbaddierer_1 (.a(a_i), .b(b_i), .s(halbaddierer_1_s), .c(halbaddierer_1_c));
  Halbaddierer halbaddierer_2 (.a(halbaddierer_1_s), .b(c_i), .s(s_i), .c(halbaddierer_2_c));
  or or_1 (c_i_plus_1, halbaddierer_1_c, halbaddierer_2_c);
endmodule
