// Digital circuit Volladdierer_enable.dig as structural Verilog
module Volladdierer_enable (
  input  a_i,
  input  b_i,
  input  c_i,
  input  EN,
  output s_i,
  output c_i_plus_1
);

  wire volladdierer_1_c_i_plus_1, volladdierer_1_s_i;

  Volladdierer volladdierer_1 (
    .a_i(a_i), .b_i(b_i), .c_i(c_i), .s_i(volladdierer_1_s_i), .c_i_plus_1(volladdierer_1_c_i_plus_1));
  and and_1 (s_i, volladdierer_1_s_i, EN);
  and and_2 (c_i_plus_1, volladdierer_1_c_i_plus_1, EN);
endmodule
