// Digital circuit half complete.dig as structural Verilog
module half_complete (
  input  CLK,
  input  RST,
  input  EN
);

  wire and_1_out, c, not_1_out, not_2_out, or_1_out, seq_1_p3, seq_1_p4, seq_1_p5;
  wire [3:0] Akku_d_out, Akku_d_out_2, IR_d_out, IR_d_out_2;
  wire [6:0] PC_a_out;
  wire [7:0] _8_bit_alu_1_output, DR_d_out, rom_1_d;
  wire [7:7] PC_a_out_2;

  not not_1 (not_1_out, c);
  and and_1 (and_1_out, CLK, EN);
  // Seq seq_1: pin names not known; wires that end beside it: not_1_out, RST, seq_1_p3, seq_1_p4, seq_1_p5
  and and_2 (c, and_1_out, ~RST);  // And
  LED led_1 (.in(seq_1_p3));
  LED led_2 (.in(seq_1_p4));
  LED led_3 (.in(seq_1_p5));
  Seven_Seg_Hex seven_seg_hex_1 (.d(IR_d_out_2), .dp(1'b1));
  _8_Bit_Register IR (.D_IN(rom_1_d), .EN(seq_1_p3), .CLK(c), .RST(RST), .D_OUT({IR_d_out_2, IR_d_out}));
  Seven_Seg_Hex seven_seg_hex_2 (.d(IR_d_out), .dp(1'b1));
  _8_Bit_Register DR (.D_IN(rom_1_d), .EN(seq_1_p4), .CLK(c), .RST(RST), .D_OUT(DR_d_out));
  Seven_Seg_Hex seven_seg_hex_3 (.d(DR_d_out[7:4]), .dp(1'b1));
  Seven_Seg_Hex seven_seg_hex_4 (.d(DR_d_out[3:0]), .dp(1'b1));
  or or_1 (or_1_out, seq_1_p3, seq_1_p4);
  \_8_Bit_Zählregister  PC (
    .A_IN({8{1'b0}}), .INC(1'b1), .EN(or_1_out), .CLK(c), .RST(RST), .A_out({PC_a_out_2[7], PC_a_out}));
  _8_Bit_ALU _8_bit_alu_1 (
    .A(DR_d_out), .B({IR_d_out_2, IR_d_out}), .c_IN(1'b0), .INVA(1'b0), .ENA(1'b1), .ENB(1'b1), .F0(1'b1),
    .F1(1'b1), .\output (_8_bit_alu_1_output));  // open: carry_out
  Seven_Seg_Hex seven_seg_hex_5 (.d(Akku_d_out_2), .dp(1'b1));
  _8_Bit_Register Akku (
    .D_IN(_8_bit_alu_1_output), .EN(seq_1_p5), .CLK(c), .RST(RST), .D_OUT({Akku_d_out_2, Akku_d_out}));
  Seven_Seg_Hex seven_seg_hex_6 (.d(Akku_d_out), .dp(1'b1));
  ROM #(.AddrBits(7), .Bits(8)) rom_1 (.A(PC_a_out), .sel(not_2_out), .D(rom_1_d));
  not not_2 (not_2_out, PC_a_out_2[7]);
  RAMDualPort #(.AddrBits(7), .Bits(8)) ramdualport_1 (
    .A(PC_a_out), .Din({8{1'b0}}), .str(1'b1), .C(c), .ld(PC_a_out_2[7]), .D(rom_1_d));

  // Other names for the same wires on the sheet: r = RST

  // Notes on the sheet:
  //   CLK: Hz: 50
  //   contents of rom_1 (hex, n*v repeats v):
  //   1,2,3,4,0,0,0,0,0,0,0,0,0,0,0,0,1
endmodule
