// Digital circuit try.dig as structural Verilog
module try (
  input  INVA,
  input  A,
  input  ENA,
  input  B,
  input  ENB,
  input  CarryIn,
  input  F0,
  input  F1
);

  wire alu_1_carry_out, alu_1_output;

  LED led_1 (.in(alu_1_output));
  LED led_2 (.in(alu_1_carry_out));
  ALU alu_1 (
    .INVA(INVA), .A(A), .ENA(ENA), .B(B), .ENB(ENB), .CarryIn(CarryIn), .F0(F0), .F1(F1),
    .\output (alu_1_output), .carry_out(alu_1_carry_out));
endmodule
